# Fritzing sketch _fritzing (saved by Fritzing 0.9.10b)
breadboards: 1

parts:
  M1 = STM32F103C8T6 blue mini board
  Q1 = NPN-Transistor [package="TO92 [THT]"]
  L1 = Inductor [package="400 mil [THT]"]
  D1 = Rectifier Diode [part_number=1N4001 package="300 mil [THT]"]
  C2 = Electrolytic Capacitor [capacitance=1µF voltage=35V package="100 mil [THT, electrolytic]"]
  R1 = Resistor [tolerance=±5% power=0.25 resistance=220 package=THT]
  R2 = Resistor [tolerance=±5% power=0.25 resistance=220 package=THT]
  C3 = Electrolytic Capacitor [capacitance=1µF voltage=35V package="100 mil [THT, electrolytic]"]

nets:
  N1: M1.A8, R1.Pin_0
  N2: M1.5V, L1.pin_1, C2.+
  N3: M1.G, Q1.E, C2.-, R2.Pin_0, C3.-
  N4: Q1.B, R1.Pin_1
  N5: Q1.C, L1.pin_0, D1.anode
  N6: D1.cathode, R2.Pin_1, C3.+
