# Fritzing sketch fritzing (saved by Fritzing 0.9.10b)
breadboards: 1

parts:
  M1 = STM32F103C8T6 blue mini board
  Q1 = NPN-Transistor [package="TO92 [THT]"]
  L1 = Inductor [package="400 mil [THT]"]
  D1 = Rectifier Diode [part_number=1N4001 package="300 mil [THT]"]
  Cin = Electrolytic Capacitor [capacitance=1µF voltage=35V package="100 mil [THT, electrolytic]"]
  Rbase = Resistor [tolerance=±5% power=0.25 resistance=220 package=THT]
  Rload = Resistor [tolerance=±5% power=0.25 resistance=220 package=THT]
  Cout = Electrolytic Capacitor [capacitance=1µF voltage=35V package="100 mil [THT, electrolytic]"]

nets:
  N1: M1.G, Q1.E, Cin.-, Rload.Pin_0, Cout.-
  N2: M1.3.3V, L1.pin_1, Cin.+
  N3: M1.A1, Rbase.Pin_0
  N4: Q1.B, Rbase.Pin_1
  N5: Q1.C, L1.pin_0, D1.anode
  N6: D1.cathode, Rload.Pin_1, Cout.+
